# Fritzing sketch Fritzing (saved by Fritzing 1.0.6)

parts:
  Part2 = Adafruit SDIO microSD Breakout
  Part3 = Adafruit MAX98357A I2S 3W Class D Amplifier [part_number="Adafruit #3006"]
  Part4 = Adafruit ESP32-S3 Feather [part_number="Adafruit #5323"]

nets:
  3.3V: Part2.3.3V, Part3.VIN, Part4.3.3V
  GND: Part2.GND, Part3.GND, Part4.GND
  N1: Part2.SCLK, Part4.A0
  N2: Part2.DO, Part4.A1
  N3: Part2.DI, Part4.A2
  N4: Part2.CS, Part4.A3
  N5: Part2.DAT1, Part4.A4
  N6: Part2.DAT2, Part4.A5
  N7: Part2.CARDDET, Part4.SCK
  N8: Part3.DIN, Part4.TX
  N9: Part3.BCLK, Part4.RX
  N10: Part3.LRCLK, Part4.MISO

custom parts:
  Adafruit MAX98357A I2S 3W Class D Amplifier: Listen to this good news - we now have an all in one digital audio amp breakout board that works incredibly well with the Raspberry Pi! If you're looking for an easy and low cost way to get you digital sound files bumpin' then the MAX08357 I2S Amp Breakout is for you. It takes standard I2S digital audio input and, not only decodes it into analog, but also amplifies it directly into a speaker.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
  Adafruit ESP32-S3 Feather: The ESP32-S3 has arrived in Feather format - and what a great way to get started with this powerful new chip from Espressif! With dual 240 MHz cores, WiFi and BLE support, and native USB, this Feather is great for powering your IoT projects. That's right - it's the new Adafruit ESP32-S3 Feather! With native USB and 8 MB flash, this board will let you upgrade your existing ESP32 projects.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
